# Fritzing sketch Arduino-RHL (saved by Fritzing 0.9.3b)
breadboards: 1

parts:
  Part1 = Arduino Mega 2560 (Rev3)
  Arduino1 = Arduino Mega Sensor Shield v2.0
  DHT1 = DHT11 Humitidy and Temperature Sensor

nets:
  N1: Part1.A8, Arduino1.A8
  N2: Part1.A9, Arduino1.A9
  N3: Part1.A10, Arduino1.A10
  N4: Part1.A11, Arduino1.A11
  N5: Part1.A12, Arduino1.A12
  N6: Part1.A13, Arduino1.A13
  N7: Part1.A14, Arduino1.A14
  N8: Part1.A15, Arduino1.A15
  N9: Part1.A0, Arduino1.A0
  N10: Part1.A1, Arduino1.A1
  N11: Part1.A2, Arduino1.A2
  N12: Part1.A3, Arduino1.A3
  N13: Part1.A4, Arduino1.A4
  N14: Part1.A5, Arduino1.A5
  N15: Part1.A6, Arduino1.A6
  N16: Part1.A7, Arduino1.A7
  N17: Part1.D21/SCL, Arduino1.21
  N18: Part1.D20/SDA, Arduino1.20
  N19: Part1.D19/RX1, Arduino1.19
  N20: Part1.D18/TX1, Arduino1.18
  N21: Part1.D17_PWM/RX2, Arduino1.17
  N22: Part1.D16_PWM/TX2, Arduino1.16
  N23: Part1.D15/RX3, Arduino1.15
  N24: Part1.D14/TX3, Arduino1.14
  N25: Part1.AREF, Arduino1.AREF
  GND: Part1.GND, Arduino1.GND
  N26: Part1.D13_PWM, Arduino1.13
  N27: Part1.D12_PWM, Arduino1.12
  N28: Part1.D11_PWM, Arduino1.11
  N29: Part1.D10_PWM, Arduino1.10
  N30: Part1.D9_PWM, Arduino1.9
  N31: Part1.D8_PWM, Arduino1.8
  N32: Part1.RESET, Arduino1.RST
  3V3: Part1.3V3, Arduino1.3V3
  5V: Part1.5V, Arduino1.5V
  VIN: Part1.VIN, Arduino1.VIN
  N33: Part1.D0_RX0, Arduino1.RX0
  N34: Part1.D1_TX0, Arduino1.TX0
  N35: Part1.D2_PWM, Arduino1.2
  N36: Part1.D3_PWM, Arduino1.3
  N37: Part1.D4_PWM, Arduino1.4
  N38: Part1.D5_PWM, Arduino1.5
  N39: Part1.D6_PWM, Arduino1.6
  N40: Part1.D7_PWM, Arduino1.7
  N41: Part1.D22, Arduino1.22
  N42: Part1.D23, Arduino1.23
  N43: Part1.D24, Arduino1.24
  N44: Part1.D25, Arduino1.25
  N45: Part1.D26, Arduino1.26
  N46: Part1.D27, Arduino1.27
  N47: Part1.D28, Arduino1.28
  N48: Part1.D29, Arduino1.29
  N49: Part1.D30, Arduino1.30
  N50: Part1.D31, Arduino1.31
  N51: Part1.D32, Arduino1.32
  N52: Part1.D33, Arduino1.33
  N53: Part1.D34, Arduino1.34
  N54: Part1.D35, Arduino1.35
  N55: Part1.D36, Arduino1.36
  N56: Part1.D37, Arduino1.37
  N57: Part1.D38, Arduino1.38
  N58: Part1.D39, Arduino1.39
  N59: Part1.D40, Arduino1.40
  N60: Part1.D41, Arduino1.41
  N61: Part1.D42, Arduino1.42
  N62: Part1.D43, Arduino1.43
  N63: Part1.D44, Arduino1.44
  N64: Part1.D45, Arduino1.45
  N65: Part1.D46, Arduino1.46
  N66: Part1.D47, Arduino1.47
  N67: Part1.D48, Arduino1.48
  N68: Part1.D49, Arduino1.49
  N69: Part1.D50, Arduino1.50
  N70: Part1.D51, Arduino1.51
  N71: Part1.D52, Arduino1.52
  N72: Part1.D53, Arduino1.53
  N73: DHT1.DATA, DHT1.NULL

custom parts:
  Arduino Mega Sensor Shield v2.0: Arduino Mega shield for multi-purpose design.
  DHT11 Humitidy and Temperature Sensor: DHT11 Humidity and Temperature Sensor

// code stored in the sketch: dht11sensor.ino
#include <DHT.h>

DHT dht43(43, DHT11);
DHT dht44(44, DHT11);
DHT dht45(45, DHT11);
DHT dht46(46, DHT11);
DHT dht47(47, DHT11);
DHT dht48(48, DHT11);
DHT dht49(49, DHT11);
DHT dht50(50, DHT11);
DHT dht51(51, DHT11);
DHT dht52(52, DHT11);

void setup() {
  Serial.begin(9600);
  setupInitDht();
}

void loop() {

    loopReadDht();
    delay(1000);

}

void setupInitDht() {
  dht43.begin();
  dht44.begin();
  dht45.begin();
  dht46.begin();
  dht47.begin();
  dht48.begin();
  dht49.begin();
  dht50.begin();
  dht51.begin();
  dht52.begin();
}

void loopReadDht() {
    /*--------43----------*/
    float h43 = dht43.readHumidity();
    float t43 = dht43.readTemperature();

    if (isnan(h43) || isnan(t43)) {
      Serial.println("I can not read the testimony 43");
//      return;
    }
    String out43 = "d43/h:"+String(h43)+"/t/"+String(t43)+"|";
    /*--------43----------*/
    /*--------44----------*/
    float h44 = dht44.readHumidity();
    float t44 = dht44.readTemperature();

    if (isnan(h44) || isnan(t44)) {
      Serial.println("I can not read the testimony 44");
//      return;
    }
    String out44 = "d44/h:"+String(h44)+"/t/"+String(t44)+"|";
    /*--------44----------*/
    /*--------45----------*/
    float h45 = dht45.readHumidity();
    float t45 = dht45.readTemperature();

    if (isnan(h45) || isnan(t45)) {
      Serial.println("I can not read the testimony 45");
//      return;
    }
    String out45 = "d45/h:"+String(h45)+"/t/"+String(t45)+"|";
    /*--------45----------*/
    /*--------46----------*/
    float h46 = dht46.readHumidity();
    float t46 = dht46.readTemperature();

    if (isnan(h46) || isnan(t46)) {
      Serial.println("I can not read the testimony 46");
//      return;
    }
    String out46 = "d46/h:"+String(h46)+"/t/"+String(t46)+"|";
    /*--------46----------*/
    /*--------47----------*/
    float h47 = dht47.readHumidity();
    float t47 = dht47.readTemperature();

    if (isnan(h47) || isnan(t47)) {
      Serial.println("I can not read the testimony 47");
//      return;
    }
    String out47 = "d47/h:"+String(h47)+"/t/"+String(t47)+"|";
    /*--------47----------*/
    /*--------48----------*/
    float h48 = dht48.readHumidity();
    float t48 = dht48.readTemperature();

    if (isnan(h48) || isnan(t48)) {
      Serial.println("I can not read the testimony 48");
//      return;
    }
    String out48 = "d48/h:"+String(h48)+"/t/"+String(t48)+"|";
    /*--------48----------*/
    /*--------49----------*/
    float h49 = dht49.readHumidity();
    float t49 = dht49.readTemperature();

    if (isnan(h49) || isnan(t49)) {
      Serial.println("I can not read the testimony 49");
//      return;
    }
    String out49 = "d49/h:"+String(h49)+"/t/"+String(t49)+"|";
    /*--------49----------*/
    /*--------50----------*/
    float h50 = dht50.readHumidity();
    float t50 = dht50.readTemperature();

    if (isnan(h50) || isnan(t50)) {
      Serial.println("I can not read the testimony 50");
//      return;
    }
    String out50 = "d50/h:"+String(h50)+"/t/"+String(t50)+"|";
    /*--------50----------*/
    /*--------51----------*/
    float h51 = dht51.readHumidity();
    float t51 = dht51.readTemperature();

    if (isnan(h51) || isnan(t51)) {
      Serial.println("I can not read the testimony 51");
//      return;
    }
    String out51 = "d51/h:"+String(h51)+"/t/"+String(t51)+"|";
    /*--------51----------*/
    /*--------52----------*/
    float h52 = dht52.readHumidity();
    float t52 = dht52.readTemperature();

    if (isnan(h52) || isnan(t52)) {
      Serial.println("I can not read the testimony 52");
      return;
    }
    String out52 = "d52/h:"+String(h52)+"/t/"+String(t52)+"|";
    /*--------52----------*/

    String out = out43+out44+out45+out46+out47+out47+out49+out50+out51+out52;
//    for(int i=46; i<=52; i++){
//      out = out + 
//    }
    Serial.println(out);
    
}

// code stored in the sketch: flashing-led.ino
/* мигающий светодиод */


int led = 13;

void setup(){
  pinMode(led, OUTPUT);
}

void loop() {
  digitalWrite(led, HIGH);
  delay(1000);
  digitalWrite(led, LOW);
  delay(1000);
}
